// Logisim project Processador_Vetorial.circ as structural Verilog: 21 circuits, main circuit Sagui_Vetorial
module Sagui_Vetorial (
);

  wire Branch_ID, Branch_ID_EX, clk_mem, clk_proc, dualram_1_p1, Flush, LI_ID, LI_ID_EX, MemWrite_EX_MEM,
       MemWrite_EX_MEM_S, MemWrite_ID, MemWrite_ID_EX, MemWrite_ID_EX_S, multiplexer_4_out,
       multiplexer_5_out, multiplexer_15_out, multiplexer_16_out, multiplexer_17_out, multiplexer_18_out,
       multiplexer_20_out, multiplexer_37_out, or_1_out, PredictTaken_ID_EX, PredictTaken_IF,
       PredictTaken_IF_ID, RegWrite_EX_MEM, RegWrite_EX_MEM_S, RegWrite_ID, RegWrite_ID_EX, RegWrite_ID_EX_S,
       RegWrite_MEM_WB, RegWrite_MEM_WB_S, Reset_EX_MEM, Reset_ID_EX, Reset_IF_ID, Stall, Taken, Taken_EX,
       Type_ID, Write_IF_ID;
  wire [1:0] ALUOp_ID, ALUOp_ID_EX, ALUOp_ID_EX_S, FwA, FwB, multiplexer_3_out, multiplexer_6_out,
       multiplexer_10_out, multiplexer_11_out, multiplexer_12_out, multiplexer_14_out, multiplexer_19_out,
       multiplexer_26_out, multiplexer_27_out, multiplexer_28_out, MUX_RegIn_EX_MEM, MUX_RegIn_EX_MEM_S,
       MUX_RegIn_ID, MUX_RegIn_ID_EX, MUX_RegIn_ID_EX_S, MUX_RegIn_MEM_WB, MUX_RegIn_MEM_WB_S, ra_ID,
       ra_ID_EX, ra_ID_EX_S, rb_ID_EX, rb_ID_EX_S, rd_EX_MEM, rd_EX_MEM_S, rd_ID_EX, rd_ID_EX_S, rd_MEM_WB,
       rd_MEM_WB_S;
  wire [3:0] Imm_ID, Imm_ID_EX, Imm_ID_EX_S, multiplexer_9_out, multiplexer_13_out, multiplexer_25_out,
       multiplexer_29_out, Opcode_ID_EX, Opcode_ID_EX_S;
  wire [7:0] adder_1_out, Data_EX_MEM, Data_WB, Data_WB_S, Endereco_Previsto_IF, Instrucao_IF, LImm_Ext_ID,
       LImm_Ext_ID_EX, MemDataOut_MEM, MemDataOut_MEM_S, MemDataOut_MEM_WB, MemDataOut_MEM_WB_S,
       multiplexer_7_out, multiplexer_8_out, multiplexer_21_out, multiplexer_22_out, multiplexer_23_out,
       multiplexer_24_out, multiplexer_35_out, multiplexer_38_out, multiplexer_39_out, PC_Next, PC_Out_ID_EX,
       PC_Out_IF, PC_Out_IF_ID, R_ra_EX, R_ra_EX_MEM, R_ra_EX_MEM_S, R_ra_EX_S, R_ra_ID, R_ra_ID_EX,
       R_ra_ID_EX_S, R_rb_EX, R_rb_EX_1_S, R_rb_EX_2, R_rb_EX_2_S, R_rb_EX_MEM, R_rb_EX_MEM_S, R_rb_ID,
       R_rb_ID_EX, R_rb_ID_EX_S, R_rb_MEM_WB_S, Reg_Mv_EX, Reg_Mv_EX_MEM, Reg_Mv_EX_MEM_S, Reg_Mv_EX_S,
       Reg_Mv_MEM_WB, Reg_Mv_MEM_WB_S, ULA_OUT_EX, ULA_OUT_EX_MEM, ULA_OUT_EX_MEM_S, ULA_OUT_EX_S,
       ULA_OUT_MEM_WB, ULA_OUT_MEM_WB_S;
  wire [7:4] Instrucao_IF_ID;

  assign LImm_Ext_ID = {{6{Imm_ID[1]}}, Imm_ID[1:0]};  // Bit_Extender bit_extender_1
  Unidade_de_Reset unidade_de_reset_1 (
    .Flush(Flush), .Stall(Stall), .clk_mem(clk_mem), .Write_IF_ID(Write_IF_ID), .Reset_IF_ID(Reset_IF_ID),
    .Reset_ID_EX(Reset_ID_EX), .Reset_EX_MEM(Reset_EX_MEM));
  Unidade_de_Controle Controle (.opcode(Instrucao_IF_ID));  // open: MUX_Type, ALUOp, MUX_ULA_B, Branch, JAR, MUX_SumPC, MemWrite, RegWrite, MUX_RegIn
  Unidade_de_Reset unidade_de_reset_2 (
    .Flush(Flush), .Stall(Stall), .clk_mem(clk_mem), .Write_IF_ID(Write_IF_ID), .Reset_IF_ID(Reset_IF_ID),
    .Reset_ID_EX(Reset_ID_EX), .Reset_EX_MEM(Reset_EX_MEM));
  Multiplexer #(.width(2)) multiplexer_1 (.in0(Imm_ID[3:2]), .in1(2'b01), .out(ra_ID), .sel(Type_ID));
  Multiplexer #(.width(2)) multiplexer_2 (.in0(Imm_ID[3:2]), .in1(2'b01), .out(ra_ID), .sel(Type_ID));
  Hazard_Detectation_Unit hazard_detectation_unit_1 (
    .Opcode_ID_EX(Opcode_ID_EX), .Opcode_ID(Instrucao_IF_ID), .ra_ID(ra_ID), .rd_ID_EX(rd_ID_EX),
    .rb_ID(Imm_ID[1:0]), .Stall(Stall));
  Hazard_Detectation_Unit hazard_detectation_unit_2 (
    .Opcode_ID_EX(Opcode_ID_EX), .Opcode_ID(Instrucao_IF_ID), .ra_ID(ra_ID), .rd_ID_EX(rd_ID_EX),
    .rb_ID(Imm_ID[1:0]), .Stall(Stall));
  Banco_de_Registradores banco_de_registradores_1 (
    .clk(clk_mem), .rd(rd_MEM_WB), .RegIn(Data_WB), .RegWrite(RegWrite_MEM_WB), .ra(ra_ID), .rb(Imm_ID[1:0]),
    .R_ra(R_ra_ID), .R_rb(R_rb_ID));
  Banco_de_Registradores banco_de_registradores_2 (
    .clk(clk_mem), .rd(rd_MEM_WB_S), .RegIn(Data_WB_S), .RegWrite(RegWrite_MEM_WB_S), .ra(ra_ID),
    .rb(Imm_ID[1:0]), .R_ra(R_ra_ID), .R_rb(R_rb_ID));
  Multiplexer #(.width(2)) multiplexer_3 (.in0(ALUOp_ID), .in1(2'b00), .out(multiplexer_3_out), .sel(Reset_ID_EX));
  Multiplexer multiplexer_4 (.in0(MemWrite_ID), .in1(1'b0), .out(multiplexer_4_out), .sel(Reset_ID_EX));
  Multiplexer multiplexer_5 (.in0(RegWrite_ID), .in1(1'b0), .out(multiplexer_5_out), .sel(Reset_ID_EX));
  Multiplexer #(.width(2)) multiplexer_6 (.in0(MUX_RegIn_ID), .in1(2'b00), .out(multiplexer_6_out), .sel(Reset_ID_EX));
  Multiplexer #(.width(8)) multiplexer_7 (.in0(R_ra_ID), .in1({8{1'b0}}), .out(multiplexer_7_out), .sel(Reset_ID_EX));
  Multiplexer #(.width(8)) multiplexer_8 (.in0(R_rb_ID), .in1({8{1'b0}}), .out(multiplexer_8_out), .sel(Reset_ID_EX));
  Multiplexer #(.width(4)) multiplexer_9 (.in0(Imm_ID), .in1(4'b0000), .out(multiplexer_9_out), .sel(Reset_ID_EX));
  Multiplexer #(.width(2)) multiplexer_10 (.in0(ra_ID), .in1(2'b00), .out(multiplexer_10_out), .sel(Reset_ID_EX));
  Multiplexer #(.width(2)) multiplexer_11 (.in0(ra_ID), .in1(2'b00), .out(multiplexer_11_out), .sel(Reset_ID_EX));
  Multiplexer #(.width(2)) multiplexer_12 (.in0(Imm_ID[1:0]), .in1(2'b00), .out(multiplexer_12_out), .sel(Reset_ID_EX));
  Multiplexer #(.width(4)) multiplexer_13 (
    .in0(Instrucao_IF_ID), .in1(4'b0100), .out(multiplexer_13_out), .sel(Reset_ID_EX));
  Multiplexer #(.width(2)) multiplexer_14 (.in0(ALUOp_ID), .in1(2'b00), .out(multiplexer_14_out), .sel(Reset_ID_EX));
  Multiplexer multiplexer_15 (.in0(Branch_ID), .in1(1'b0), .out(multiplexer_15_out), .sel(Reset_ID_EX));
  Multiplexer multiplexer_16 (.in0(LI_ID), .in1(1'b0), .out(multiplexer_16_out), .sel(Reset_ID_EX));
  Multiplexer multiplexer_17 (.in0(MemWrite_ID), .in1(1'b0), .out(multiplexer_17_out), .sel(Reset_ID_EX));
  Multiplexer multiplexer_18 (.in0(RegWrite_ID), .in1(1'b0), .out(multiplexer_18_out), .sel(Reset_ID_EX));
  Multiplexer #(.width(2)) multiplexer_19 (
    .in0(MUX_RegIn_ID), .in1(2'b00), .out(multiplexer_19_out), .sel(Reset_ID_EX));
  Multiplexer multiplexer_20 (.in0(PredictTaken_IF_ID), .in1(1'b0), .out(multiplexer_20_out), .sel(Reset_ID_EX));
  Multiplexer #(.width(8)) multiplexer_21 (
    .in0(PC_Out_IF_ID), .in1({8{1'b0}}), .out(multiplexer_21_out), .sel(Reset_ID_EX));
  Multiplexer #(.width(8)) multiplexer_22 (.in0(R_ra_ID), .in1({8{1'b0}}), .out(multiplexer_22_out), .sel(Reset_ID_EX));
  Multiplexer #(.width(8)) multiplexer_23 (.in0(R_rb_ID), .in1({8{1'b0}}), .out(multiplexer_23_out), .sel(Reset_ID_EX));
  Multiplexer #(.width(8)) multiplexer_24 (
    .in0(LImm_Ext_ID), .in1({8{1'b0}}), .out(multiplexer_24_out), .sel(Reset_ID_EX));
  Multiplexer #(.width(4)) multiplexer_25 (.in0(Imm_ID), .in1(4'b0000), .out(multiplexer_25_out), .sel(Reset_ID_EX));
  Multiplexer #(.width(2)) multiplexer_26 (.in0(ra_ID), .in1(2'b00), .out(multiplexer_26_out), .sel(Reset_ID_EX));
  Multiplexer #(.width(2)) multiplexer_27 (.in0(ra_ID), .in1(2'b00), .out(multiplexer_27_out), .sel(Reset_ID_EX));
  Multiplexer #(.width(2)) multiplexer_28 (.in0(Imm_ID[1:0]), .in1(2'b00), .out(multiplexer_28_out), .sel(Reset_ID_EX));
  Multiplexer #(.width(4)) multiplexer_29 (
    .in0(Instrucao_IF_ID), .in1(4'b0100), .out(multiplexer_29_out), .sel(Reset_ID_EX));
  Register #(.width(2)) register_1 (.D(multiplexer_3_out), .Q(ALUOp_ID_EX), .clk(clk_proc));  // open: en, clr
  Register #(.width(1)) register_2 (.D(multiplexer_4_out), .Q(MemWrite_ID_EX), .clk(clk_proc));  // open: en, clr
  Register #(.width(1)) register_3 (.D(multiplexer_5_out), .Q(RegWrite_ID_EX), .clk(clk_proc));  // open: en, clr
  Register #(.width(2)) register_4 (.D(multiplexer_6_out), .Q(MUX_RegIn_ID_EX), .clk(clk_proc));  // open: en, clr
  Register register_5 (.D(multiplexer_7_out), .Q(R_ra_ID_EX), .clk(clk_proc));  // open: en, clr
  Register register_6 (.D(multiplexer_8_out), .Q(R_rb_ID_EX), .clk(clk_proc));  // open: en, clr
  Register #(.width(4)) register_7 (.D(multiplexer_9_out), .Q(Imm_ID_EX), .clk(clk_proc));  // open: en, clr
  Register #(.width(2)) register_8 (.D(multiplexer_10_out), .Q(rd_ID_EX), .clk(clk_proc));  // open: en, clr
  Register #(.width(2)) register_9 (.D(multiplexer_11_out), .Q(ra_ID_EX), .clk(clk_proc));  // open: en, clr
  Register #(.width(2)) register_10 (.D(multiplexer_12_out), .Q(rb_ID_EX), .clk(clk_proc));  // open: en, clr
  Register #(.width(4)) register_11 (.D(multiplexer_13_out), .Q(Opcode_ID_EX), .clk(clk_proc));  // open: en, clr
  Register #(.width(2)) u_ALUop_ID_EX_S (.D(multiplexer_14_out), .Q(ALUOp_ID_EX_S), .clk(clk_proc));  // open: en, clr
  Register #(.width(1)) u_Branch_ID_EX (.D(multiplexer_15_out), .Q(Branch_ID_EX), .clk(clk_proc));  // open: en, clr
  Register #(.width(1)) u_LI_ID_EX (.D(multiplexer_16_out), .Q(LI_ID_EX), .clk(clk_proc));  // open: en, clr
  Register #(.width(1)) u_MemWrite_ID_EX_S (
    .D(multiplexer_17_out), .Q(MemWrite_ID_EX_S), .clk(clk_proc));  // open: en, clr
  Register #(.width(1)) u_RegWrite_ID_EX_S (
    .D(multiplexer_18_out), .Q(RegWrite_ID_EX_S), .clk(clk_proc));  // open: en, clr
  Register #(.width(2)) u_MUX_RegIn_ID_EX_S (
    .D(multiplexer_19_out), .Q(MUX_RegIn_ID_EX_S), .clk(clk_proc));  // open: en, clr
  Register #(.width(1)) u_PredictTaken_ID_EX (
    .D(multiplexer_20_out), .Q(PredictTaken_ID_EX), .clk(clk_proc));  // open: en, clr
  Register u_PC_Out_ID_EX (.D(multiplexer_21_out), .Q(PC_Out_ID_EX), .clk(clk_proc));  // open: en, clr
  Register u_R_ra_ID_EX_S (.D(multiplexer_22_out), .Q(R_ra_ID_EX_S), .clk(clk_proc));  // open: en, clr
  Register u_R_rb_ID_EX_S (.D(multiplexer_23_out), .Q(R_rb_ID_EX_S), .clk(clk_proc));  // open: en, clr
  Register u_LImm_Ext_ID_EX (.D(multiplexer_24_out), .Q(LImm_Ext_ID_EX), .clk(clk_proc));  // open: en, clr
  Register #(.width(4)) u_Imm_ID_EX_S (.D(multiplexer_25_out), .Q(Imm_ID_EX_S), .clk(clk_proc));  // open: en, clr
  Register #(.width(2)) u_rd_ID_EX_S (.D(multiplexer_26_out), .Q(rd_ID_EX_S), .clk(clk_proc));  // open: en, clr
  Register #(.width(2)) u_ra_ID_EX_S (.D(multiplexer_27_out), .Q(ra_ID_EX_S), .clk(clk_proc));  // open: en, clr
  Register #(.width(2)) u_rb_ID_EX_S (.D(multiplexer_28_out), .Q(rb_ID_EX_S), .clk(clk_proc));  // open: en, clr
  Register #(.width(4)) u_Opcode_ID_EX_S (.D(multiplexer_29_out), .Q(Opcode_ID_EX_S), .clk(clk_proc));  // open: en, clr
  Unidade_Forwarding unidade_forwarding_1 (
    .RegWrite_MEM_WB(RegWrite_MEM_WB), .RegWrite_EX_MEM(RegWrite_EX_MEM), .ra_ID_EX(ra_ID_EX_S),
    .rb_ID_EX(rb_ID_EX_S), .rd_MEM(rd_EX_MEM), .rd_WB(rd_MEM_WB), .Opcode_ID_EX(Opcode_ID_EX_S),
    .ULA_Out_EX_MEM(ULA_OUT_EX_MEM), .Reg_mv_EX_MEM(Reg_Mv_EX_MEM), .MUX_RegIn_EX_MEM(MUX_RegIn_EX_MEM),
    .FwA(FwA), .FwB(FwB), .Data_EX_MEM(Data_EX_MEM));
  Multiplexer #(.width(8)) multiplexer_30 (.in0(R_rb_ID_EX_S), .in1(LImm_Ext_ID_EX), .out(R_rb_EX_1_S), .sel(LI_ID_EX));
  Unidade_Forwarding unidade_forwarding_2 (
    .RegWrite_MEM_WB(RegWrite_MEM_WB), .RegWrite_EX_MEM(RegWrite_EX_MEM), .ra_ID_EX(ra_ID_EX),
    .rb_ID_EX(rb_ID_EX), .rd_MEM(rd_EX_MEM), .rd_WB(rd_MEM_WB), .Opcode_ID_EX(Opcode_ID_EX),
    .ULA_Out_EX_MEM(ULA_OUT_EX_MEM), .Reg_mv_EX_MEM(Reg_Mv_EX_MEM), .MUX_RegIn_EX_MEM(MUX_RegIn_EX_MEM),
    .FwA(FwA), .FwB(FwB), .Data_EX_MEM(Data_EX_MEM));
  Multiplexer #(.select(2), .width(8)) multiplexer_31 (
    .in0(R_ra_ID_EX_S), .in1(Data_EX_MEM), .in2(Data_WB_S), .out(R_ra_EX_S), .sel(FwA));  // open: in3
  Multiplexer #(.select(2), .width(8)) multiplexer_32 (
    .in0(R_rb_EX_1_S), .in1(Data_EX_MEM), .in2(Data_WB_S), .out(R_rb_EX_2_S), .sel(FwB));  // open: in3
  Multiplexer #(.select(2), .width(8)) multiplexer_33 (
    .in0(R_ra_ID_EX), .in1(Data_EX_MEM), .in2(Data_WB), .out(R_ra_EX), .sel(FwA));  // open: in3
  Multiplexer #(.select(2), .width(8)) multiplexer_34 (
    .in0(R_rb_ID_EX), .in1(Data_EX_MEM), .in2(Data_WB), .out(R_rb_EX), .sel(FwB));  // open: in3
  Branch_Control branch_control_1 (.Branch(Branch_ID_EX), .R_ra(R_ra_EX_S), .Taken(Taken_EX));
  ULA_S ula_s_1 (.ULA_A(R_ra_EX_S), .ULA_B(R_rb_EX_2_S), .ALUOp(ALUOp_ID_EX_S), .ULA_OUT(ULA_OUT_EX_S));
  Juntador juntador_1 (.R_ra(R_ra_EX_S), .Imm(Imm_ID_EX_S), .Opcode(Opcode_ID_EX_S), .Reg_Moved(Reg_Mv_EX_S));
  BTB_e_Preditor btb_e_preditor_1 (
    .clk(clk_proc), .Taken_EX(Taken_EX), .Branch_ID_EX(Branch_ID_EX), .R_rb(R_rb_EX_2),
    .PC_Out_ID_EX(PC_Out_ID_EX), .PC_Out_IF(PC_Out_IF), .PredictTaken(PredictTaken_IF),
    .Endereco_Previsto(Endereco_Previsto_IF));
  ULA_V ula_v_1 (.ULA_A(R_ra_EX), .ULA_B(R_rb_EX), .ALUOp(ALUOp_ID_EX[0]), .ULA_OUT(ULA_OUT_EX));
  Juntador juntador_2 (.R_ra(R_ra_EX), .Imm(Imm_ID_EX), .Opcode(Opcode_ID_EX), .Reg_Moved(Reg_Mv_EX));
  xor xor_1 (Flush, PredictTaken_ID_EX, Taken);
  Adder adder_1 (.a(PC_Out_IF), .b(8'h1), .out(adder_1_out));  // open: cin, cout
  Multiplexer #(.width(8)) multiplexer_35 (
    .in0(adder_1_out), .in1(Endereco_Previsto_IF), .out(multiplexer_35_out), .sel(PredictTaken_IF));
  Multiplexer #(.width(8)) multiplexer_36 (.in0(multiplexer_35_out), .in1(R_rb_EX_2), .out(PC_Next), .sel(Flush));
  Register register_12 (.D(ULA_OUT_EX), .Q(ULA_OUT_EX_MEM), .clk(clk_proc), .clr(Reset_EX_MEM));  // open: en
  Register register_13 (.D(R_ra_EX), .Q(R_ra_EX_MEM), .clk(clk_proc), .clr(Reset_EX_MEM));  // open: en
  Register register_14 (.D(R_rb_EX), .Q(R_rb_EX_MEM), .clk(clk_proc), .clr(Reset_EX_MEM));  // open: en
  Register #(.width(2)) register_15 (.D(rd_ID_EX), .Q(rd_EX_MEM), .clk(clk_proc), .clr(Reset_EX_MEM));  // open: en
  Register register_16 (.D(Reg_Mv_EX), .Q(Reg_Mv_EX_MEM), .clk(clk_proc), .clr(Reset_EX_MEM));  // open: en
  Register #(.width(1)) register_17 (
    .D(MemWrite_ID_EX), .Q(MemWrite_EX_MEM), .clk(clk_proc), .clr(Reset_EX_MEM));  // open: en
  Register #(.width(1)) register_18 (
    .D(RegWrite_ID_EX), .Q(RegWrite_EX_MEM), .clk(clk_proc), .clr(Reset_EX_MEM));  // open: en
  Register #(.width(2)) register_19 (
    .D(MUX_RegIn_ID_EX), .Q(MUX_RegIn_EX_MEM), .clk(clk_proc), .clr(Reset_EX_MEM));  // open: en
  Register u_ULA_OUT_EX_MEM_S (.D(ULA_OUT_EX_S), .Q(ULA_OUT_EX_MEM_S), .clk(clk_proc), .clr(Reset_EX_MEM));  // open: en
  Register u_R_ra_EX_MEM_S (.D(R_ra_EX_S), .Q(R_ra_EX_MEM_S), .clk(clk_proc), .clr(Reset_EX_MEM));  // open: en
  Register u_R_rb_EX_MEM_S (.D(R_rb_EX_2_S), .Q(R_rb_EX_MEM_S), .clk(clk_proc), .clr(Reset_EX_MEM));  // open: en
  Register #(.width(2)) u_rd_EX_MEM_S (
    .D(rd_ID_EX_S), .Q(rd_EX_MEM_S), .clk(clk_proc), .clr(Reset_EX_MEM));  // open: en
  Register u_Reg_Mv_EX_MEM_S (.D(Reg_Mv_EX_S), .Q(Reg_Mv_EX_MEM_S), .clk(clk_proc), .clr(Reset_EX_MEM));  // open: en
  Register #(.width(1)) u_MemWrite_EX_MEM_S (
    .D(MemWrite_ID_EX_S), .Q(MemWrite_EX_MEM_S), .clk(clk_proc), .clr(Reset_EX_MEM));  // open: en
  Register #(.width(1)) u_RegWrite_EX_MEM_S (
    .D(RegWrite_ID_EX_S), .Q(RegWrite_EX_MEM_S), .clk(clk_proc), .clr(Reset_EX_MEM));  // open: en
  Register #(.width(2)) u_MUX_RegIn_EX_MEM_S (
    .D(MUX_RegIn_ID_EX_S), .Q(MUX_RegIn_EX_MEM_S), .clk(clk_proc), .clr(Reset_EX_MEM));  // open: en
  or or_1 (or_1_out, Flush, ~Stall);  // OR_Gate
  PC pc_1 (.PC_In(PC_Next), .PCWrite(or_1_out), .clk(clk_proc), .PC_Out(PC_Out_IF));
  Clock #(.phaseOffset(3)) clock_1 (.out(clk_mem));
  Clock #(.highDuration(2), .lowDuration(2), .phaseOffset(3)) clock_2 (.out(clk_proc));
  Clock #(.phaseOffset(3)) u_clk_mem (.out(clk_mem));
  Clock #(.highDuration(2), .lowDuration(2), .phaseOffset(3)) clk_processador (.out(clk_proc));
  RAM ram_1 (
    .addr(R_rb_EX_MEM), .we(MemWrite_EX_MEM), .oe(1'b1), .clk(clk_mem), .din(R_ra_EX_MEM),
    .dout(MemDataOut_MEM));
  // Digital_Oscilloscope digital_oscilloscope_1: pin names not known; wires that end beside it: clk_mem, clk_proc
  // DualRAM #(.asyncread("true"), .clearpin("true")) dualram_1: pin names not known; wires that end beside it: dualram_1_p1, PC_Out_IF, 1'b0, 1'b1, clk_mem, {8{1'b0}}, R_rb_EX_MEM_S, MemWrite_EX_MEM_S, 1'b1, clk_mem, R_ra_EX_MEM_S, Instrucao_IF, MemDataOut_MEM_S
  // Digital_Oscilloscope digital_oscilloscope_2: pin names not known; wires that end beside it: clk_mem, clk_proc
  Multiplexer multiplexer_37 (.in0(PredictTaken_IF), .in1(1'b0), .out(multiplexer_37_out), .sel(Reset_IF_ID));
  Multiplexer #(.width(8)) multiplexer_38 (
    .in0(PC_Out_IF), .in1({8{1'b0}}), .out(multiplexer_38_out), .sel(Reset_IF_ID));
  Multiplexer #(.width(8)) multiplexer_39 (
    .in0(Instrucao_IF), .in1(8'h64), .out(multiplexer_39_out), .sel(Reset_IF_ID));
  Register #(.width(1)) register_20 (.D(RegWrite_EX_MEM), .Q(RegWrite_MEM_WB), .clk(clk_proc));  // open: en, clr
  Register #(.width(2)) register_21 (.D(MUX_RegIn_EX_MEM), .Q(MUX_RegIn_MEM_WB), .clk(clk_proc));  // open: en, clr
  Register register_22 (.D(ULA_OUT_EX_MEM), .Q(ULA_OUT_MEM_WB), .clk(clk_proc));  // open: en, clr
  Register register_23 (.D(MemDataOut_MEM), .Q(MemDataOut_MEM_WB), .clk(clk_proc));  // open: en, clr
  Register register_24 (.D(Reg_Mv_EX_MEM), .Q(Reg_Mv_MEM_WB), .clk(clk_proc));  // open: en, clr
  Register #(.width(2)) register_25 (.D(rd_EX_MEM), .Q(rd_MEM_WB), .clk(clk_proc));  // open: en, clr
  Register #(.width(1)) u_PredictTaken_IF_ID (
    .D(multiplexer_37_out), .en(Write_IF_ID), .Q(PredictTaken_IF_ID), .clk(clk_proc));  // open: clr
  Register u_PC_Out_IF_ID (.D(multiplexer_38_out), .en(Write_IF_ID), .Q(PC_Out_IF_ID), .clk(clk_proc));  // open: clr
  Register u_Instrucao_IF_ID (
    .D(multiplexer_39_out), .en(Write_IF_ID), .Q({Instrucao_IF_ID, Imm_ID}), .clk(clk_proc));  // open: clr
  Register #(.width(1)) u_RegWrite_MEM_WB_S (
    .D(RegWrite_EX_MEM_S), .Q(RegWrite_MEM_WB_S), .clk(clk_proc));  // open: en, clr
  Register #(.width(2)) u_MUX_RegIn_MEM_WB_S (
    .D(MUX_RegIn_EX_MEM_S), .Q(MUX_RegIn_MEM_WB_S), .clk(clk_proc));  // open: en, clr
  Register u_ULA_Out_MEM_WB_S (.D(ULA_OUT_EX_MEM_S), .Q(ULA_OUT_MEM_WB_S), .clk(clk_proc));  // open: en, clr
  Register u_MemDataOut_MEM_WB_S (.D(MemDataOut_MEM_S), .Q(MemDataOut_MEM_WB_S), .clk(clk_proc));  // open: en, clr
  Register u_Reg_Mv_MEM_WB_S (.D(Reg_Mv_EX_MEM_S), .Q(Reg_Mv_MEM_WB_S), .clk(clk_proc));  // open: en, clr
  Register u_R_rb_MEM_WB_S (.D(R_rb_EX_MEM_S), .Q(R_rb_MEM_WB_S), .clk(clk_proc));  // open: en, clr
  Register #(.width(2)) u_rd_MEM_WB_S (.D(rd_EX_MEM_S), .Q(rd_MEM_WB_S), .clk(clk_proc));  // open: en, clr
  Multiplexer #(.select(2), .width(8)) multiplexer_40 (
    .in0(ULA_OUT_MEM_WB), .in1(MemDataOut_MEM_WB), .in2(Reg_Mv_MEM_WB), .out(Data_WB), .sel(MUX_RegIn_MEM_WB));  // open: in3
  Multiplexer #(.select(2), .width(8)) multiplexer_41 (
    .in0(ULA_OUT_MEM_WB_S), .in1(MemDataOut_MEM_WB_S), .in2(Reg_Mv_MEM_WB_S), .in3(R_rb_MEM_WB_S),
    .out(Data_WB_S), .sel(MUX_RegIn_MEM_WB_S));
  // Pins of 1 and 2 bits meet at ALUOp_ID_EX

  // Other names for the same wires on the sheet: ALUOp_ID_S[1:0] = ALUOp_ID; ALUOp_ID_V = ALUOp_ID[0];
  //   Instrucao_IF_ID[3:0] = Imm_ID; rb_ID[1:0] = Imm_ID[1:0]; ra[1:0] = Imm_ID[3:2];
  //   Opcode_ID[3:0] = Instrucao_IF_ID

  // Notes on the sheet:
  //   I. DECODE (ID)
  //   I. DECODE (ID)
  //   É Move?
  //   Se for, ra e rd igual a 1
  //   É Move?
  //   Se for, ra e rd igual a 1
  //   ID/EX
  //   ID/EX
  //   Dado é adiantado? Daonde?
  //   Dado é adiantado? Daonde?
  //   EXECUTE (EX)
  //   EXECUTE (EX)
  //   Previção Certa?
  //   Cálculo de PC_Next: PC + 1 ou Endereço Previsto ou Correção de Salto
  //   EX/MEM
  //   EX/MEM
  //   I. FETCH (IF)
  //   Memória de Instruções
  //   MEMORY (MEM)
  //   Memória de Dados
  //   MEMORY (MEM)
  //   MEM/WB
  //   IF/ID
  //   MEM/WB
  //   WRITE BACK (WB)
  //   WRITE BACK (WB)
endmodule

module Banco_de_Registradores (
  input  clk,
  input  [1:0] rd,
  input  [7:0] RegIn,
  input  RegWrite,
  input  [1:0] ra,
  input  [1:0] rb,
  output [7:0] R_ra,
  output [7:0] R_rb
);

  wire [7:0] registradores_1_r_r0, registradores_1_r_r1, registradores_1_r_r2, registradores_1_r_r3;

  Registradores registradores_1 (
    .RegWrite(RegWrite), .rd(rd), .RegIn(RegIn), .clk(clk), .R_r0(registradores_1_r_r0),
    .R_r1(registradores_1_r_r1), .R_r2(registradores_1_r_r2), .R_r3(registradores_1_r_r3));
  Multiplexer #(.select(2), .width(8)) multiplexer_1 (
    .in0(registradores_1_r_r0), .in1(registradores_1_r_r1), .in2(registradores_1_r_r2),
    .in3(registradores_1_r_r3), .out(R_ra), .sel(ra));
  Multiplexer #(.select(2), .width(8)) multiplexer_2 (
    .in0(registradores_1_r_r0), .in1(registradores_1_r_r1), .in2(registradores_1_r_r2),
    .in3(registradores_1_r_r3), .out(R_rb), .sel(rb));
endmodule

module Registradores (
  input  RegWrite,
  input  [1:0] rd,
  input  [7:0] RegIn,
  input  clk,
  output [7:0] R_r0,
  output [7:0] R_r1,
  output [7:0] R_r2,
  output [7:0] R_r3
);

  wire demultiplexer_1_out1, demultiplexer_1_out2, demultiplexer_1_out3;

  Demultiplexer #(.select(2)) demultiplexer_1 (
    .out1(demultiplexer_1_out1), .out2(demultiplexer_1_out2), .out3(demultiplexer_1_out3), .in(RegWrite),
    .sel(rd));  // open: out0
  Register r0 (.D({8{1'b0}}), .en(1'b0), .clk(clk), .Q(R_r0));  // open: clr
  Register r1 (.D(RegIn), .en(demultiplexer_1_out1), .clk(clk), .Q(R_r1));  // open: clr
  Register r2 (.D(RegIn), .en(demultiplexer_1_out2), .clk(clk), .Q(R_r2));  // open: clr
  Register r3 (.D(RegIn), .en(demultiplexer_1_out3), .clk(clk), .Q(R_r3));  // open: clr

  // Notes on the sheet:
  //   Se ele não for resetado pelo reset, então tem que permitir escrita
endmodule

module PC (
  input  [7:0] PC_In,
  input  PCWrite,
  input  clk,
  output [7:0] PC_Out
);

  Register register_1 (.D(PC_In), .en(PCWrite), .clk(clk), .Q(PC_Out));  // open: clr
endmodule

module ULA_S (
  input  [7:0] ULA_A,
  input  [7:0] ULA_B,
  input  [1:0] ALUOp,
  output [7:0] ULA_OUT
);

  wire [7:0] adder_1_out, and_1_out, subtractor_1_out;

  Adder adder_1 (.a(ULA_A), .b(ULA_B), .out(adder_1_out));  // open: cin, cout
  Subtractor subtractor_1 (.a(ULA_A), .b(ULA_B), .out(subtractor_1_out));  // open: bin, bout
  assign and_1_out = ULA_A & ULA_B;  // AND_Gate and_1, 8 bits wide
  Multiplexer #(.select(2), .width(8)) multiplexer_1 (
    .in0(adder_1_out), .in1(subtractor_1_out), .in2(and_1_out), .out(ULA_OUT), .sel(ALUOp));  // open: in3
endmodule

module Branch_Control (
  input  Branch,
  input  [7:0] R_ra,
  output Taken
);

  wire nor_1_out;

  and and_1 (Taken, Branch, nor_1_out);
  nor nor_1 (nor_1_out, R_ra[0], R_ra[1], R_ra[2], R_ra[3], R_ra[4], R_ra[5], R_ra[6], R_ra[7]);

  // Notes on the sheet:
  //   Se 'for branch' e R[r0] == 0 OU 'for salto incondional', então desvie
endmodule

module Proximo_PC (
  input  MUX_PC,
  input  [7:0] PC_OUT,
  input  [7:0] Imm_Ext,
  input  [7:0] R_rb,
  input  MUX_SumPC,
  output [7:0] PC_In
);

  wire [7:0] adder_1_out, multiplexer_1_out;

  Multiplexer #(.width(8)) multiplexer_1 (.in0(8'h1), .in1(Imm_Ext), .out(multiplexer_1_out), .sel(MUX_SumPC));
  Multiplexer #(.width(8)) multiplexer_2 (.in0(adder_1_out), .in1(R_rb), .out(PC_In), .sel(MUX_PC));
  Adder adder_1 (.a(PC_OUT), .b(multiplexer_1_out), .out(adder_1_out));  // open: cin, cout
endmodule

module Shifter_Left (
  input  [7:0] ULA_A,
  input  [7:0] ULA_B,
  output [7:0] ULA_OUT
);

  wire or_1_out;
  wire [7:0] shifter_1_out;

  Shifter shifter_1 (.in(ULA_A), .\dist (ULA_B[2:0]), .out(shifter_1_out));
  Multiplexer #(.width(8)) multiplexer_1 (.in0(shifter_1_out), .in1({8{1'b0}}), .out(ULA_OUT), .sel(or_1_out));
  or or_1 (or_1_out, ULA_B[3], ULA_B[4], ULA_B[5], ULA_B[6], ULA_B[7]);

  // Notes on the sheet:
  //   Se o shift tiver overflow, então o resultado do shift será 0
endmodule

module Shift_Right (
  input  [7:0] ULA_A,
  input  [7:0] ULA_B,
  output [7:0] ULA_OUT
);

  wire or_1_out;
  wire [7:0] shifter_1_out;

  Shifter #(.shift("lr")) shifter_1 (.in(ULA_A), .\dist (ULA_B[2:0]), .out(shifter_1_out));
  Multiplexer #(.width(8)) multiplexer_1 (.in0(shifter_1_out), .in1({8{1'b0}}), .out(ULA_OUT), .sel(or_1_out));
  or or_1 (or_1_out, ULA_B[3], ULA_B[4], ULA_B[5], ULA_B[6], ULA_B[7]);

  // Notes on the sheet:
  //   Se o shift tiver overflow, então o resultado do shift será 0
endmodule

module Unidade_de_Controle (
  input  [3:0] opcode,
  output MUX_Type,
  output [2:0] ALUOp,
  output MUX_ULA_B,
  output Branch,
  output JAR,
  output MUX_SumPC,
  output MemWrite,
  output RegWrite,
  output [1:0] MUX_RegIn
);

  wire and_1_out, and_2_out, and_3_out, and_4_out, and_5_out, and_10_out, and_11_out, and_12_out, and_13_out,
       not_1_out, not_2_out, not_3_out, not_4_out;

  not not_1 (not_1_out, opcode[3]);
  not not_2 (not_2_out, opcode[2]);
  not not_3 (not_3_out, opcode[1]);
  not not_4 (not_4_out, opcode[0]);
  and and_1 (and_1_out, not_1_out, not_3_out, opcode[0]);
  and and_2 (and_2_out, not_1_out, opcode[2], not_4_out);
  and and_3 (and_3_out, not_1_out, not_3_out);
  and and_4 (and_4_out, not_1_out, opcode[0]);
  and and_5 (and_5_out, not_1_out, opcode[2]);
  and and_6 (Branch, not_1_out, not_2_out, not_3_out, not_4_out);
  and and_7 (JAR, not_1_out, opcode[2], opcode[1], opcode[0]);
  and and_8 (MUX_SumPC, not_1_out, not_2_out, not_3_out, opcode[0]);
  and and_9 (MemWrite, not_1_out, not_2_out, opcode[1], opcode[0]);
  and and_10 (and_10_out, opcode[1], not_4_out);
  and and_11 (and_11_out, opcode[2], not_3_out);
  and and_12 (and_12_out, not_1_out, opcode[0]);
  and and_13 (and_13_out, not_1_out, opcode[2], opcode[1]);
  and and_14 (MUX_RegIn[0], not_1_out, opcode[1]);
  or or_1 (MUX_Type, and_1_out, and_2_out);
  or or_2 (MUX_ULA_B, and_3_out, and_4_out, and_5_out);
  or or_3 (RegWrite, and_10_out, and_11_out, opcode[3]);
  or or_4 (MUX_RegIn[1], and_12_out, and_13_out);

  assign ALUOp = opcode[2:0];
endmodule

module Teste_clk (
);

  wire clock_1_out, clock_2_out;

  Clock #(.phaseOffset(3)) clock_1 (.out(clock_1_out));
  Clock #(.highDuration(2), .lowDuration(2), .phaseOffset(3)) clock_2 (.out(clock_2_out));
  // Digital_Oscilloscope digital_oscilloscope_1: pin names not known; wires that end beside it: clock_1_out, clock_2_out
endmodule

module Controle_Forwading (
  input  ra_igual_rd_MEM,
  input  rb_igual_rd_MEM,
  input  ra_igual_rd_WB,
  input  rb_igual_rd_WB,
  output [1:0] ForwardA,
  output [1:0] ForwardB
);

  wire not_1_out, not_2_out;

  not not_1 (not_1_out, ra_igual_rd_MEM);
  not not_2 (not_2_out, rb_igual_rd_MEM);
  and and_1 (ForwardA[1], not_1_out, ra_igual_rd_WB);
  and and_2 (ForwardB[1], not_2_out, rb_igual_rd_WB);

  assign ForwardA[0] = ra_igual_rd_MEM;
  assign ForwardB[0] = rb_igual_rd_MEM;
endmodule

// UnidadeFowarding
module Unidade_Forwarding (
  input  RegWrite_MEM_WB,
  input  RegWrite_EX_MEM,
  input  [1:0] ra_ID_EX,
  input  [1:0] rb_ID_EX,
  input  [1:0] rd_MEM,
  input  [1:0] rd_WB,
  input  [3:0] Opcode_ID_EX,
  input  [7:0] ULA_Out_EX_MEM,
  input  [7:0] Reg_mv_EX_MEM,
  input  [1:0] MUX_RegIn_EX_MEM,
  output [1:0] FwA,
  output [1:0] FwB,
  output [7:0] Data_EX_MEM
);

  wire and_1_out, and_2_out, and_3_out, and_4_out, comparator_1_eq, comparator_2_eq, comparator_3_eq,
       comparator_4_eq, detector_de_leitura_1_regreada, detector_de_leitura_1_regreadb, undriven;
  wire [1:0] controle_forwading_1_forwarda, controle_forwading_1_forwardb;

  Comparator #(.width(2)) comparator_1 (.a(ra_ID_EX), .b(rd_MEM), .eq(comparator_1_eq));  // open: gt, lt
  Comparator #(.width(2)) comparator_2 (.a(rb_ID_EX), .b(rd_MEM), .eq(comparator_2_eq));  // open: gt, lt
  Comparator #(.width(2)) comparator_3 (.a(ra_ID_EX), .b(rd_WB), .eq(comparator_3_eq));  // open: gt, lt
  Comparator #(.width(2)) comparator_4 (.a(rb_ID_EX), .b(rd_WB), .eq(comparator_4_eq));  // open: gt, lt
  Multiplexer #(.width(8)) multiplexer_1 (.out(Data_EX_MEM), .sel(undriven));  // open: in0, in1
  and and_1 (and_1_out, RegWrite_EX_MEM, comparator_1_eq);
  and and_2 (and_2_out, RegWrite_EX_MEM, comparator_2_eq);
  and and_3 (and_3_out, RegWrite_MEM_WB, comparator_3_eq);
  and and_4 (and_4_out, RegWrite_MEM_WB, comparator_4_eq);
  Controle_Forwading controle_forwading_1 (
    .ra_igual_rd_MEM(and_1_out), .rb_igual_rd_MEM(and_2_out), .ra_igual_rd_WB(and_3_out),
    .rb_igual_rd_WB(and_4_out), .ForwardA(controle_forwading_1_forwarda),
    .ForwardB(controle_forwading_1_forwardb));
  Detector_de_Leitura detector_de_leitura_1 (
    .Opcode(Opcode_ID_EX), .RegReadA(detector_de_leitura_1_regreada),
    .RegReadB(detector_de_leitura_1_regreadb));
  Multiplexer #(.width(2)) multiplexer_2 (
    .in0(2'b00), .in1(controle_forwading_1_forwarda), .out(FwA), .sel(detector_de_leitura_1_regreada));
  Multiplexer #(.width(2)) multiplexer_3 (
    .in0(2'b00), .in1(controle_forwading_1_forwardb), .out(FwB), .sel(detector_de_leitura_1_regreadb));

  // Notes on the sheet:
  //   RegWrite
endmodule

module Detector_de_Leitura (
  input  [3:0] Opcode,
  output RegReadA,
  output RegReadB
);

  wire and_1_out, and_2_out, and_3_out, and_4_out, and_5_out, and_6_out, and_7_out, and_8_out, and_9_out,
       not_1_out, not_2_out, not_3_out, not_4_out;

  not not_1 (not_1_out, Opcode[3]);
  not not_2 (not_2_out, Opcode[2]);
  not not_3 (not_3_out, Opcode[1]);
  not not_4 (not_4_out, Opcode[0]);
  and and_1 (and_1_out, not_2_out, Opcode[1]);
  and and_2 (and_2_out, Opcode[3], Opcode[0]);
  and and_3 (and_3_out, not_1_out, not_3_out, not_4_out);
  and and_4 (and_4_out, Opcode[3], Opcode[2]);
  and and_5 (and_5_out, not_1_out, not_2_out, not_4_out);
  and and_6 (and_6_out, Opcode[1], Opcode[0]);
  and and_7 (and_7_out, Opcode[3], Opcode[0]);
  and and_8 (and_8_out, Opcode[3], Opcode[2]);
  and and_9 (and_9_out, not_2_out, Opcode[1]);
  or or_1 (RegReadA, and_1_out, and_2_out, and_3_out, and_4_out);
  or or_2 (RegReadB, and_5_out, and_6_out, and_7_out, and_8_out, and_9_out);
endmodule

module Hazard_Detectation_Unit (
  input  [3:0] Opcode_ID_EX,
  input  [3:0] Opcode_ID,
  input  [1:0] ra_ID,
  input  [1:0] rd_ID_EX,
  input  [1:0] rb_ID,
  output Stall
);

  wire and_1_out, and_2_out, and_3_out, comparator_1_eq, comparator_2_eq, detector_de_leitura_1_regreada,
       detector_de_leitura_1_regreadb, or_1_out;

  and and_1 (and_1_out, ~Opcode_ID_EX[0], Opcode_ID_EX[1], ~Opcode_ID_EX[2], ~Opcode_ID_EX[3]);  // AND_Gate
  Comparator #(.width(2)) comparator_1 (.a(ra_ID), .b(rd_ID_EX), .eq(comparator_1_eq));  // open: gt, lt
  Comparator #(.width(2)) comparator_2 (.a(rd_ID_EX), .b(rb_ID), .eq(comparator_2_eq));  // open: gt, lt
  Detector_de_Leitura detector_de_leitura_1 (
    .Opcode(Opcode_ID), .RegReadA(detector_de_leitura_1_regreada), .RegReadB(detector_de_leitura_1_regreadb));
  and and_2 (and_2_out, detector_de_leitura_1_regreada, comparator_1_eq);
  and and_3 (and_3_out, detector_de_leitura_1_regreadb, comparator_2_eq);
  or or_1 (or_1_out, and_2_out, and_3_out);
  and and_4 (Stall, and_1_out, or_1_out);

  // Notes on the sheet:
  //   É Load
  //   Existe dependência
  //   Stall
endmodule

module BTB_e_Preditor (
  input  clk,
  input  Taken_EX,
  input  Branch_ID_EX,
  input  [7:0] R_rb,
  input  [7:0] PC_Out_ID_EX,
  input  [7:0] PC_Out_IF,
  output PredictTaken,
  output [7:0] Endereco_Previsto
);

  wire Bit_de_Validade, comparator_1_eq, Estado;
  wire [0:0] Estado_Atual;
  wire [1:0] NovoEstado;
  wire [3:0] BTB_Endereco, Index;

  Multiplexer #(.width(4)) multiplexer_1 (
    .in0(PC_Out_IF[3:0]), .in1(PC_Out_ID_EX[3:0]), .out(Index), .sel(Branch_ID_EX));
  RAM #(.addrWidth(4), .asyncread("true"), .dataWidth(4)) Endereco_Instrucao (
    .addr(Index), .we(Branch_ID_EX), .oe(1'b1), .clk(clk), .din(PC_Out_ID_EX[7:4]), .dout(BTB_Endereco));
  RAM #(.addrWidth(4), .asyncread("true")) Endereco_Desvio (
    .addr(Index), .we(Branch_ID_EX), .oe(1'b1), .clk(clk), .din(R_rb), .dout(Endereco_Previsto));
  RAM #(.addrWidth(4), .asyncread("true"), .dataWidth(1)) Validade (
    .addr(Index), .we(Branch_ID_EX), .oe(1'b1), .clk(clk), .din(1'b1), .dout(Bit_de_Validade));
  RAM #(.addrWidth(4), .asyncread("true"), .dataWidth(2)) u_Estado (
    .addr(Index), .we(Branch_ID_EX), .oe(1'b1), .clk(clk), .din(NovoEstado), .dout({Estado, Estado_Atual[0]}));
  Novo_Estado novo_estado_1 (.Estado_Atual({Estado, Estado_Atual[0]}), .Taken(Taken_EX), .Novo_Estado(NovoEstado));
  Comparator #(.width(4)) comparator_1 (.a(BTB_Endereco), .b(PC_Out_IF[7:4]), .eq(comparator_1_eq));  // open: gt, lt
  and and_1 (PredictTaken, Estado, Bit_de_Validade, ~Branch_ID_EX, comparator_1_eq);  // AND_Gate

  // Other names for the same wires on the sheet: Branch_EX = Branch_ID_EX; Estado_Atual[1] = Estado;
  //   PC_Out_ID_EX_0_3[3:0] = PC_Out_ID_EX[3:0]; PC_Out_ID_EX_4_7[3:0] = PC_Out_ID_EX[7:4];
  //   PC_Out_IF_0_3[3:0] = PC_Out_IF[3:0]; PC_Out_IF_4_7[3:0] = PC_Out_IF[7:4]; PC_Salto_EX[7:0] = R_rb

  // Notes on the sheet:
  //   Se  branch no execute -> Circuito esté escrevendo
  //   Caso contrário -> Circuito está lendo a Cache e verificando se há predição
  //   Taken?
  //   Valid?
  //   Esta lendo?
  //   Hit?
endmodule

module Novo_Estado (
  input  [1:0] Estado_Atual,
  input  Taken,
  output [1:0] Novo_Estado
);

  wire and_1_out, and_2_out, and_3_out, and_4_out, and_5_out, and_6_out, not_1_out;

  not not_1 (not_1_out, Estado_Atual[0]);
  and and_1 (and_1_out, Estado_Atual[0], Taken);
  and and_2 (and_2_out, Estado_Atual[1], Taken);
  and and_3 (and_3_out, Estado_Atual[1], Estado_Atual[0]);
  and and_4 (and_4_out, not_1_out, Taken);
  and and_5 (and_5_out, Estado_Atual[1], not_1_out);
  and and_6 (and_6_out, Estado_Atual[1], Taken);
  or or_1 (Novo_Estado[1], and_1_out, and_2_out, and_3_out);
  or or_2 (Novo_Estado[0], and_4_out, and_5_out, and_6_out);
endmodule

module Unidade_de_Reset (
  input  Flush,
  input  Stall,
  input  clk_mem,
  output Write_IF_ID,
  output Reset_IF_ID,
  output Reset_ID_EX,
  output Reset_EX_MEM
);

  wire and_1_out, not_1_out, or_1_out;

  Reset_Inicial reset_inicial_1 (.clk_mem(clk_mem), .Reset(Reset_EX_MEM));
  not not_1 (not_1_out, Flush);
  or or_1 (or_1_out, Stall, Flush);
  and and_1 (and_1_out, not_1_out, Stall);
  not not_2 (Write_IF_ID, and_1_out);
  or or_2 (Reset_ID_EX, or_1_out, Reset_EX_MEM);

  assign Reset_IF_ID = Flush;

  // Other names for the same wires on the sheet: ResetInicial = Reset_EX_MEM
endmodule

module Reset_Inicial (
  input  clk_mem,
  output Reset
);

  wire and_1_out, not_2_out, or_1_out, Z0, Z1;

  not not_1 (Reset, Z1);
  not not_2 (not_2_out, Z0);
  or or_1 (or_1_out, Z0, Z1);
  and and_1 (and_1_out, not_2_out, Reset);
  D_Flip_Flop d_ff_1 (.D(or_1_out), .clk(clk_mem), .Q(Z1));  // open: Qn, preset, reset
  D_Flip_Flop d_ff_2 (.D(and_1_out), .clk(clk_mem), .Q(Z0));  // open: Qn, preset, reset
endmodule

module Juntador (
  input  [7:0] R_ra,
  input  [3:0] Imm,
  input  [3:0] Opcode,
  output [7:0] Reg_Moved
);

  Multiplexer #(.width(8)) multiplexer_1 (
    .in0({Imm, R_ra[3:0]}), .in1({R_ra[7:4], Imm}), .out(Reg_Moved), .sel(Opcode[0]));

  // Notes on the sheet:
  //   MOVE HIGH
  //   MOVE LOW
endmodule

module ULA_V (
  input  [7:0] ULA_A,
  input  [7:0] ULA_B,
  input  ALUOp,
  output [7:0] ULA_OUT
);

  wire [7:0] adder_1_out, subtractor_1_out;

  Adder adder_1 (.a(ULA_A), .b(ULA_B), .out(adder_1_out));  // open: cin, cout
  Subtractor subtractor_1 (.a(ULA_A), .b(ULA_B), .out(subtractor_1_out));  // open: bin, bout
  Multiplexer #(.width(8)) multiplexer_1 (.in0(adder_1_out), .in1(subtractor_1_out), .out(ULA_OUT), .sel(ALUOp));
endmodule
