// Logisim project vliw.circ as structural Verilog: 12 circuits, main circuit VLIW
module VLIW (
  input  RST
);

  wire CLK, decodificador_1_branch, decodificador_1_condition, decodificador_1_jr,
       decodificador_1_l1regwrite, decodificador_1_memread, decodificador_1_memwrite,
       decodificador_1_mux_imm, decodificador_1_mux_regin, decodificador_1_mux_ula_bl3,
       decodificador_1_mux_ula_bl4, decodificador_1_regwritel3, decodificador_1_regwritel4,
       decodificador_1_relative, decodificador_1_tipo_i_lane1, decodificador_1_tipo_i_lane2, Flush,
       L1_MUX_RegIn, L1_RegWrite, l1MuxRegin, l1RegWrite, L3RegWrite, L3RegWrite2, L4RegWrite, L4RegWrite2,
       or_1_out, registrador_id_ex_1_branchs, registrador_id_ex_1_jrs, registrador_id_ex_1_l2conditions,
       registrador_id_ex_1_l3mux_ula_bs, registrador_id_ex_1_l4mux_ula_bs, registrador_id_ex_1_memreads,
       registrador_id_ex_1_memwrites, registrador_id_ex_1_mux_imms, registrador_id_ex_1_relatives, Tipo_I_L1,
       Tipo_I_L2, Tipo_I_L12, Tipo_I_L22;
  wire [1:0] decodificador_1_rd_l1, decodificador_1_rd_l3, decodificador_1_rd_l4, decodificador_1_sel_lane1,
       multiplexer_2_out, multiplexer_3_out, ra_L2addr, rb_addr, rb_L2addr, Rd_L1, rd_l1_t, Rd_L3, rd_l3_t,
       Rd_L4, rd_l4_t, ReadAddr1, ReadAddr2, ReadAddr3, ReadAddr4, ReadAddr5, ReadAddr6, ReadAddr7,
       ReadAddr8, registrador_id_ex_1_sel_lane1s;
  wire [2:0] decodificador_1_aluopl3, decodificador_1_aluopl4, registrador_id_ex_1_l3aluop_0s,
       registrador_id_ex_1_l4aluop_0s;
  wire [3:0] decodificador_1_imm_l1, decodificador_1_imm_l2, decodificador_1_imm_l3, decodificador_1_imm_l4,
       registrador_id_ex_1_l1s, registrador_id_ex_1_l2s, registrador_id_ex_1_l3s, registrador_id_ex_1_l4s;
  wire [7:0] adder_1_out, lan1_out, lane_1_1_lane1_out, multiplexer_1_out, multiplexer_4_out, NewPc, PC1,
       PC_q, R0_out, ReadData1, ReadData2, ReadData3, ReadData4, ReadData5, ReadData6, ReadData7, ReadData8,
       registrador_id_ex_1_l1_ras, registrador_id_ex_1_l1_rbs, registrador_id_ex_1_l2_ras,
       registrador_id_ex_1_l2_rbs, registrador_id_ex_1_l3_ras, registrador_id_ex_1_l3_rbs,
       registrador_id_ex_1_l4_ras, registrador_id_ex_1_l4_rbs, registrador_id_ex_1_pc1s, ULA_A,
       ULA_A_resultado, ULA_B, ULA_B_resultado;
  wire [31:0] instmem_1_instout, registrador_if_id_1_decoder;

  Multiplexer #(.width(8)) multiplexer_1 (.in0(adder_1_out), .in1(NewPc), .out(multiplexer_1_out), .sel(Flush));
  Register PC (.D(multiplexer_1_out), .en(1'b1), .clk(CLK), .Q(PC_q), .clr(RST));
  Clock u_CLK (.out(CLK));
  Adder adder_1 (.a(PC_q), .b(8'h1), .out(adder_1_out));  // open: cin, cout
  InstMem instmem_1 (.Address(PC_q), .InstOut(instmem_1_instout));
  Multiplexer #(.width(2)) multiplexer_2 (.in0(rd_l1_t), .in1(2'b00), .out(multiplexer_2_out), .sel(Tipo_I_L12));
  or or_1 (or_1_out, L3RegWrite2, L4RegWrite2);
  Multiplexer #(.width(2)) multiplexer_3 (.in0(rd_l3_t), .in1(rd_l4_t), .out(multiplexer_3_out), .sel(L3RegWrite2));
  Registrador_IF_ID registrador_if_id_1 (
    .ROM(instmem_1_instout), .PC(adder_1_out), .Flush(Flush), .Clock(CLK), .rst(RST),
    .Decoder(registrador_if_id_1_decoder), .PC1(PC1));
  Multiplexer #(.width(8)) multiplexer_4 (.in0(ULA_A), .in1(ULA_B), .out(multiplexer_4_out), .sel(L3RegWrite2));
  reg_bank reg_bank_1 (
    .WrData1(lan1_out), .WrData2(multiplexer_4_out), .ReadAddr1(ReadAddr1), .clk(CLK), .ReadAddr2(ReadAddr2),
    .rst(RST), .ReadAddr3(ReadAddr3), .ReadAddr4(ReadAddr4), .ReadAddr5(ReadAddr5), .ReadAddr6(ReadAddr6),
    .ReadAddr7(ReadAddr7), .ReadAddr8(ReadAddr8), .WrAddr1(multiplexer_2_out), .WE1(L1_RegWrite),
    .WE2(or_1_out), .WrAddr2(multiplexer_3_out), .ReadData1(ReadData1), .ReadData2(ReadData2),
    .ReadData3(ReadData3), .ReadData4(ReadData4), .ReadData5(ReadData5), .ReadData6(ReadData6),
    .ReadData7(ReadData7), .ReadData8(ReadData8), .R0_out(R0_out));
  Decodificador decodificador_1 (
    .Instr_32b(registrador_if_id_1_decoder), .RdAddr_L1_Ra(ReadAddr1), .RdAddr_L2_Ra(ReadAddr3),
    .RdAddr_L3_Ra(ReadAddr5), .RdAddr_L4_Ra(ReadAddr7), .RdAddr_L1_Rb(ReadAddr2), .RdAddr_L2_Rb(ReadAddr4),
    .RdAddr_L3_Rb(ReadAddr6), .RdAddr_L4_Rb(ReadAddr8), .Rd_L1(decodificador_1_rd_l1),
    .Rd_L3(decodificador_1_rd_l3), .Rd_L4(decodificador_1_rd_l4), .Imm_L1(decodificador_1_imm_l1),
    .Imm_L2(decodificador_1_imm_l2), .Imm_L3(decodificador_1_imm_l3), .Imm_L4(decodificador_1_imm_l4),
    .Sel_lane1(decodificador_1_sel_lane1), .MUX_Imm(decodificador_1_mux_imm),
    .MemRead(decodificador_1_memread), .MemWrite(decodificador_1_memwrite),
    .l1RegWrite(decodificador_1_l1regwrite), .Mux_RegIn(decodificador_1_mux_regin),
    .Condition(decodificador_1_condition), .Relative(decodificador_1_relative), .JR(decodificador_1_jr),
    .Branch(decodificador_1_branch), .MUX_ULA_BL3(decodificador_1_mux_ula_bl3),
    .RegWriteL3(decodificador_1_regwritel3), .ALUOpL3(decodificador_1_aluopl3),
    .MUX_ULA_BL4(decodificador_1_mux_ula_bl4), .RegWriteL4(decodificador_1_regwritel4),
    .ALUOpL4(decodificador_1_aluopl4), .Tipo_I_lane1(decodificador_1_tipo_i_lane1),
    .Tipo_i_lane2(decodificador_1_tipo_i_lane2));
  Registrador_ID_EX registrador_id_ex_1 (
    .L1_Ra(ReadData1), .L1_Rb(ReadData2), .L2_Ra(ReadData3), .L2_Rb(ReadData4), .L3_Ra(ReadData5),
    .L3_Rb(ReadData6), .L4_Ra(ReadData7), .L4_Rb(ReadData8), .PC1(PC1), .L2(decodificador_1_imm_l2),
    .L1(decodificador_1_imm_l1), .L4(decodificador_1_imm_l4), .L3(decodificador_1_imm_l3),
    .Rd_L4(decodificador_1_rd_l4), .Rd_L3(decodificador_1_rd_l3), .Rd_L1(decodificador_1_rd_l1),
    .Relative(decodificador_1_relative), .JR(decodificador_1_jr), .Branch(decodificador_1_branch),
    .MUX_Imm(decodificador_1_mux_imm), .MUX_RegIn(decodificador_1_mux_regin),
    .L1RegWrite(decodificador_1_l1regwrite), .MemWrite(decodificador_1_memwrite),
    .MemRead(decodificador_1_memread), .L4MUX_ULA_B(decodificador_1_mux_ula_bl4),
    .L4RegWrite(decodificador_1_regwritel4), .L3AluOp_0(decodificador_1_aluopl3[0]),
    .L3AluOp_1(decodificador_1_aluopl3[1]), .L3AluOp_2(decodificador_1_aluopl3[2]),
    .L3MUX_ULA_B(decodificador_1_mux_ula_bl3), .L3RegWrite(decodificador_1_regwritel3),
    .L2Condition(decodificador_1_condition), .Tipo_I_2(decodificador_1_tipo_i_lane2),
    .Tipo_I_L1(decodificador_1_tipo_i_lane1), .Sel_Lane1(decodificador_1_sel_lane1),
    .L4AluOp_0(decodificador_1_aluopl4[0]), .L4AluOp_1(decodificador_1_aluopl4[1]),
    .L4AluOp_2(decodificador_1_aluopl4[2]), .CLK(CLK), .Flush(Flush), .rst(RST),
    .L1_RaS(registrador_id_ex_1_l1_ras), .L1_RbS(registrador_id_ex_1_l1_rbs),
    .L2_RaS(registrador_id_ex_1_l2_ras), .L2_RbS(registrador_id_ex_1_l2_rbs),
    .L3_RaS(registrador_id_ex_1_l3_ras), .L3_RbS(registrador_id_ex_1_l3_rbs),
    .L4_RaS(registrador_id_ex_1_l4_ras), .L4_RbS(registrador_id_ex_1_l4_rbs),
    .PC1S(registrador_id_ex_1_pc1s), .L2S(registrador_id_ex_1_l2s), .L1S(registrador_id_ex_1_l1s),
    .L4S(registrador_id_ex_1_l4s), .L3S(registrador_id_ex_1_l3s), .Rd_L4S(Rd_L4), .Rd_L3S(Rd_L3),
    .Rd_L1S(Rd_L1), .RelativeS(registrador_id_ex_1_relatives), .JRS(registrador_id_ex_1_jrs),
    .BranchS(registrador_id_ex_1_branchs), .MUX_ImmS(registrador_id_ex_1_mux_imms), .MUX_RegInS(l1MuxRegin),
    .L1RegWriteS(l1RegWrite), .MemWriteS(registrador_id_ex_1_memwrites),
    .MemReadS(registrador_id_ex_1_memreads), .L4MUX_ULA_BS(registrador_id_ex_1_l4mux_ula_bs),
    .L4Reg_WriteS(L4RegWrite), .L3ALUOp_0S(registrador_id_ex_1_l3aluop_0s[0]),
    .L3ALUOp_1S(registrador_id_ex_1_l3aluop_0s[1]), .L3ALUOp_2S(registrador_id_ex_1_l3aluop_0s[2]),
    .L3MUX_ULA_BS(registrador_id_ex_1_l3mux_ula_bs), .L3RegWriteS(L3RegWrite),
    .L2ConditionS(registrador_id_ex_1_l2conditions), .Tipo_I_L2S(Tipo_I_L2), .Tipo_I_L1S(Tipo_I_L1),
    .Sel_lane1S(registrador_id_ex_1_sel_lane1s), .L4ALUOp_0S(registrador_id_ex_1_l4aluop_0s[0]),
    .L4ALUOp_1S(registrador_id_ex_1_l4aluop_0s[1]), .L4ALUOp_2S(registrador_id_ex_1_l4aluop_0s[2]));
  Extensao_reg_id_ex extensao_reg_id_ex_1 (
    .RdAddr_l2_ra(ReadAddr3), .RdAddr_l2_rb(ReadAddr4), .RdAddr_l1_rb(ReadAddr2), .CLK(CLK), .Flush(Flush),
    .rst(RST), .ra_l2_addr(ra_L2addr), .rb_l2_addr(rb_L2addr), .rb_addr(rb_addr));
  lane_1 lane_1_1 (
    .Ra_data(registrador_id_ex_1_l1_ras), .Rb_data(registrador_id_ex_1_l1_rbs),
    .MemWrite(registrador_id_ex_1_memwrites), .MemRead(registrador_id_ex_1_memreads),
    .Sel_lane1(registrador_id_ex_1_sel_lane1s), .Mux_Imm(registrador_id_ex_1_mux_imms), .clk(CLK),
    .Imm(registrador_id_ex_1_l1s), .fwd_lane1_out(lan1_out), .fwd_l1regWrite(L1_RegWrite), .rb_addr(rb_addr),
    .fwd_rd_l1(rd_l1_t), .lane1_out(lane_1_1_lane1_out));
  ULA_VLIW u_ULA_A (
    .Ra(registrador_id_ex_1_l3_ras), .Rb(registrador_id_ex_1_l3_rbs), .Imm(registrador_id_ex_1_l3s),
    .MUX_ULA_B(registrador_id_ex_1_l3mux_ula_bs), .ALUOp(registrador_id_ex_1_l3aluop_0s),
    .Resultado(ULA_A_resultado));
  ULA_VLIW u_ULA_B (
    .Ra(registrador_id_ex_1_l4_ras), .Rb(registrador_id_ex_1_l4_rbs), .Imm(registrador_id_ex_1_l4s),
    .MUX_ULA_B(registrador_id_ex_1_l4mux_ula_bs), .ALUOp(registrador_id_ex_1_l4aluop_0s),
    .Resultado(ULA_B_resultado));
  lane_2 lane_2_1 (
    .Ra(registrador_id_ex_1_l2_ras), .Rb(registrador_id_ex_1_l2_rbs), .R0(R0_out),
    .Imm(registrador_id_ex_1_l2s), .PC1(registrador_id_ex_1_pc1s), .Branch(registrador_id_ex_1_branchs),
    .JR(registrador_id_ex_1_jrs), .Relative(registrador_id_ex_1_relatives),
    .Condition(registrador_id_ex_1_l2conditions), .fwd_lane1_out(lan1_out), .l1_regwrite(L1_RegWrite),
    .rd_l1(rd_l1_t), .rb_addrL2(rb_L2addr), .ra_addrL2(ra_L2addr), .NewPC(NewPc), .Flush(Flush));
  Registrador_EX_WB registrador_ex_wb_1 (
    .lane1_out(lane_1_1_lane1_out), .ULA_A(ULA_A_resultado), .ULA_B(ULA_B_resultado),
    .L1_MUX_RegIn(l1MuxRegin), .L1_RegWrite(l1RegWrite), .Rd_L4(Rd_L4), .Rd_L3(Rd_L3), .Rd_L1(Rd_L1),
    .Tipo_I_L1(Tipo_I_L1), .Tipo_I_L2(Tipo_I_L2), .L4_RegWrite(L4RegWrite), .L3_RegWrite(L3RegWrite),
    .CLK(CLK), .rst(RST), .lane1_outS(lan1_out), .ULA_AS(ULA_A), .ULA_BS(ULA_B),
    .L1_MUX_RegInS(L1_MUX_RegIn), .L1_RegWriteS(L1_RegWrite), .Rd_L4S(rd_l4_t), .Rd_L3S(rd_l3_t),
    .Rd_L1S(rd_l1_t), .Tipo_I_L1S(Tipo_I_L12), .Tipo_I_L2S(Tipo_I_L22), .L4_RegWriteS(L4RegWrite2),
    .L3_RegWriteS(L3RegWrite2));

  // Notes on the sheet:
  //   MUX PC
  //   ESTÁGIO IF
  //   PC +1
  //   MUX WrAddr2
  //   REGISTRADOR IF/ID
  //   MUX_TIPO_INSTRUCAO_LANE1
  //   Mux WrData2
  //   ESTÁGIO ID
  //   REGISTRADOR ID/EX
  //   ESTÁGIO EX
  //   REGISTRADOR EX/WB
  //   ESTÁGIO WB
endmodule

module reg_bank (
  input  [7:0] WrData1,
  input  [7:0] WrData2,
  input  [1:0] ReadAddr1,
  input  clk,
  input  [1:0] ReadAddr2,
  input  rst,
  input  [1:0] ReadAddr3,
  input  [1:0] ReadAddr4,
  input  [1:0] ReadAddr5,
  input  [1:0] ReadAddr6,
  input  [1:0] ReadAddr7,
  input  [1:0] ReadAddr8,
  input  [1:0] WrAddr1,
  input  WE1,
  input  WE2,
  input  [1:0] WrAddr2,
  output [7:0] ReadData1,
  output [7:0] ReadData2,
  output [7:0] ReadData3,
  output [7:0] ReadData4,
  output [7:0] ReadData5,
  output [7:0] ReadData6,
  output [7:0] ReadData7,
  output [7:0] ReadData8,
  output [7:0] R0_out
);

  wire AND_1A, AND_1B, AND_1C, AND_1D, AND_2A, AND_2B, AND_2C, AND_2D, decoder_1_out0, decoder_1_out1,
       decoder_1_out2, decoder_1_out3, decoder_2_out0, decoder_2_out1, decoder_2_out2, decoder_2_out3, EN0,
       EN1, EN2, EN3;
  wire [7:0] R0_D, R1_D, R1_q, R2_D, R2_q, R3_D, R3_q;

  Decoder #(.enable("false"), .select(2)) decoder_1 (
    .out0(decoder_1_out0), .out1(decoder_1_out1), .out2(decoder_1_out2), .out3(decoder_1_out3), .sel(WrAddr1));
  Decoder #(.enable("false"), .select(2)) decoder_2 (
    .out0(decoder_2_out0), .out1(decoder_2_out1), .out2(decoder_2_out2), .out3(decoder_2_out3), .sel(WrAddr2));
  Multiplexer #(.width(8)) multiplexer_1 (.in0(WrData1), .in1(WrData2), .out(R0_D), .sel(AND_2A));
  Multiplexer #(.width(8)) multiplexer_2 (.in0(WrData1), .in1(WrData2), .out(R1_D), .sel(AND_2B));
  Multiplexer #(.width(8)) multiplexer_3 (.in0(WrData1), .in1(WrData2), .out(R2_D), .sel(AND_2C));
  Multiplexer #(.width(8)) multiplexer_4 (.in0(WrData1), .in1(WrData2), .out(R3_D), .sel(AND_2D));
  and and_1 (AND_1A, decoder_1_out0, WE1);
  and and_2 (AND_1B, decoder_1_out1, WE1);
  and and_3 (AND_1C, decoder_1_out2, WE1);
  and and_4 (AND_1D, decoder_1_out3, WE1);
  and and_5 (AND_2A, decoder_2_out0, WE2);
  and and_6 (AND_2B, decoder_2_out1, WE2);
  and and_7 (AND_2C, decoder_2_out2, WE2);
  and and_8 (AND_2D, decoder_2_out3, WE2);
  or or_1 (EN0, AND_1A, AND_2A);
  or or_2 (EN1, AND_1B, AND_2B);
  or or_3 (EN2, AND_1C, AND_2C);
  or or_4 (EN3, AND_1D, AND_2D);
  Register R0 (.D(R0_D), .en(EN0), .clk(clk), .Q(R0_out), .clr(rst));
  Register R1 (.D(R1_D), .en(EN1), .clk(clk), .Q(R1_q), .clr(rst));
  Register R2 (.D(R2_D), .en(EN2), .clk(clk), .Q(R2_q), .clr(rst));
  Register R3 (.D(R3_D), .en(EN3), .clk(clk), .Q(R3_q), .clr(rst));
  Multiplexer #(.select(2), .width(8)) multiplexer_5 (
    .in0(R0_out), .in1(R1_q), .in2(R2_q), .in3(R3_q), .out(ReadData1), .sel(ReadAddr1));
  Multiplexer #(.select(2), .width(8)) multiplexer_6 (
    .in0(R0_out), .in1(R1_q), .in2(R2_q), .in3(R3_q), .out(ReadData2), .sel(ReadAddr2));
  Multiplexer #(.select(2), .width(8)) multiplexer_7 (
    .in0(R0_out), .in1(R1_q), .in2(R2_q), .in3(R3_q), .out(ReadData3), .sel(ReadAddr3));
  Multiplexer #(.select(2), .width(8)) multiplexer_8 (
    .in0(R0_out), .in1(R1_q), .in2(R2_q), .in3(R3_q), .out(ReadData4), .sel(ReadAddr4));
  Multiplexer #(.select(2), .width(8)) multiplexer_9 (
    .in0(R0_out), .in1(R1_q), .in2(R2_q), .in3(R3_q), .out(ReadData5), .sel(ReadAddr5));
  Multiplexer #(.select(2), .width(8)) multiplexer_10 (
    .in0(R0_out), .in1(R1_q), .in2(R2_q), .in3(R3_q), .out(ReadData6), .sel(ReadAddr6));
  Multiplexer #(.select(2), .width(8)) multiplexer_11 (
    .in0(R0_out), .in1(R1_q), .in2(R2_q), .in3(R3_q), .out(ReadData7), .sel(ReadAddr7));
  Multiplexer #(.select(2), .width(8)) multiplexer_12 (
    .in0(R0_out), .in1(R1_q), .in2(R2_q), .in3(R3_q), .out(ReadData8), .sel(ReadAddr8));
endmodule

module ULA_VLIW (
  input  [7:0] Ra,
  input  [7:0] Rb,
  input  [3:0] Imm,
  input  MUX_ULA_B,
  input  [2:0] ALUOp,
  output [7:0] Resultado
);

  wire not_1_out, or_2_out, or_3_out, or_4_out;
  wire [7:0] B_sel, bit_extender_1_out, bit_extender_2_out, koggestone8bit_1_soma, multiplexer_2_out,
       multiplexer_3_out, or_1_out, shifter_1_out, shifter_2_out, subtractor_1_out;

  assign bit_extender_1_out = {{4{Imm[3]}}, Imm};  // Bit_Extender bit_extender_1
  Multiplexer #(.width(8)) multiplexer_1 (.in0(Rb), .in1(bit_extender_1_out), .out(B_sel), .sel(MUX_ULA_B));
  Subtractor subtractor_1 (.a(Ra), .b(B_sel), .out(subtractor_1_out));  // open: bin, bout
  assign or_1_out = Ra | B_sel;  // OR_Gate or_1, 8 bits wide
  or or_2 (or_2_out, B_sel[0], B_sel[1], B_sel[2], B_sel[3], B_sel[4], B_sel[5], B_sel[6], B_sel[7]);
  not not_1 (not_1_out, or_2_out);
  Shifter shifter_1 (.in(Ra), .\dist (B_sel[2:0]), .out(shifter_1_out));
  or or_3 (or_3_out, B_sel[3], B_sel[4], B_sel[5], B_sel[6], B_sel[7]);
  Shifter #(.shift("lr")) shifter_2 (.in(Ra), .\dist (B_sel[2:0]), .out(shifter_2_out));
  or or_4 (or_4_out, B_sel[3], B_sel[4], B_sel[5], B_sel[6], B_sel[7]);
  KoggeStone8Bit koggestone8bit_1 (.A(Ra), .B(B_sel), .Soma(koggestone8bit_1_soma));  // open: Cout
  assign bit_extender_2_out = {{7{not_1_out}}, not_1_out};  // Bit_Extender bit_extender_2
  Multiplexer #(.width(8)) multiplexer_2 (
    .in0(shifter_1_out), .in1({8{1'b0}}), .out(multiplexer_2_out), .sel(or_3_out));
  Multiplexer #(.width(8)) multiplexer_3 (
    .in0(shifter_2_out), .in1({8{1'b0}}), .out(multiplexer_3_out), .sel(or_4_out));
  Multiplexer #(.select(3), .width(8)) multiplexer_4 (
    .in0(koggestone8bit_1_soma), .in1(subtractor_1_out), .in2(or_1_out), .in3(bit_extender_2_out),
    .in4(multiplexer_2_out), .in5(multiplexer_3_out), .in6({8{1'b0}}), .in7({8{1'b0}}), .out(Resultado),
    .sel(ALUOp));
endmodule

module lane_1 (
  input  [7:0] Ra_data,
  input  [7:0] Rb_data,
  input  MemWrite,
  input  MemRead,
  input  [1:0] Sel_lane1,
  input  Mux_Imm,
  input  clk,
  input  [3:0] Imm,
  input  [7:0] fwd_lane1_out,
  input  fwd_l1regWrite,
  input  [1:0] rb_addr,
  input  [1:0] fwd_rd_l1,
  output [7:0] lane1_out
);

  wire comparator_1_eq, rb_sel;
  wire [3:0] movh;
  wire [7:0] Imediato_montado, MemOut, Rb;
  wire [7:4] movl;

  Multiplexer #(.width(8)) multiplexer_1 (.in0(Rb_data), .in1(fwd_lane1_out), .out(Rb), .sel(rb_sel));
  Multiplexer #(.width(8)) multiplexer_2 (.in0(Ra_data), .in1(fwd_lane1_out), .out({movl, movh}), .sel(fwd_l1regWrite));
  Comparator #(.width(2)) comparator_1 (.a(rb_addr), .b(fwd_rd_l1), .eq(comparator_1_eq));  // open: gt, lt
  and and_1 (rb_sel, fwd_l1regWrite, comparator_1_eq);
  RAM ram_1 (.addr(Rb), .we(MemWrite), .oe(MemRead), .clk(clk), .din(Ra_data), .dout(MemOut));
  Multiplexer #(.width(8)) multiplexer_3 (.in0({movl, Imm}), .in1({Imm, movh}), .out(Imediato_montado), .sel(Mux_Imm));
  Multiplexer #(.select(2), .width(8)) multiplexer_4 (
    .in0(MemOut), .in1(Imediato_montado), .in2(Rb), .in3({8{1'b0}}), .out(lane1_out), .sel(Sel_lane1));

  // Other names for the same wires on the sheet: fwd_lane1out[7:0] = fwd_lane1_out; movh[7:4] = Imm; movl[3:0] = Imm;
  //   Ra[7:0] = Ra_data
endmodule

module lane_2 (
  input  [7:0] Ra,
  input  [7:0] Rb,
  input  [7:0] R0,
  input  [3:0] Imm,
  input  [7:0] PC1,
  input  Branch,
  input  JR,
  input  Relative,
  input  Condition,
  input  [7:0] fwd_lane1_out,
  input  l1_regwrite,
  input  [1:0] rd_l1,
  input  [1:0] rb_addrL2,
  input  [1:0] ra_addrL2,
  output [7:0] NewPC,
  output Flush
);

  wire and_3_out, comparator_1_eq, comparator_2_eq, ra_sel, rb_sel, Zero;
  wire [7:0] adder_1_out, bit_extender_1_out, multiplexer_1_out, multiplexer_2_out, multiplexer_3_out;

  Multiplexer #(.width(8)) multiplexer_1 (.in0(Rb), .in1(fwd_lane1_out), .out(multiplexer_1_out), .sel(rb_sel));
  Comparator #(.width(2)) comparator_1 (.a(rd_l1), .b(rb_addrL2), .eq(comparator_1_eq));  // open: gt, lt
  Comparator #(.width(2)) comparator_2 (.a(rd_l1), .b(ra_addrL2), .eq(comparator_2_eq));  // open: gt, lt
  Multiplexer #(.width(8)) multiplexer_2 (.in0(Ra), .in1(fwd_lane1_out), .out(multiplexer_2_out), .sel(ra_sel));
  and and_1 (rb_sel, l1_regwrite, comparator_1_eq);
  and and_2 (ra_sel, l1_regwrite, comparator_2_eq);
  Multiplexer #(.width(8)) multiplexer_3 (.in0(multiplexer_2_out), .in1(R0), .out(multiplexer_3_out), .sel(Condition));
  assign bit_extender_1_out = {{4{Imm[3]}}, Imm};  // Bit_Extender bit_extender_1
  and and_3 (and_3_out, Branch, Zero);
  nor nor_1 (Zero, multiplexer_3_out[0], multiplexer_3_out[1], multiplexer_3_out[2], multiplexer_3_out[3], multiplexer_3_out[4], multiplexer_3_out[5], multiplexer_3_out[6], multiplexer_3_out[7]);
  Adder adder_1 (.a(bit_extender_1_out), .b(PC1), .out(adder_1_out));  // open: cin, cout
  Multiplexer #(.width(8)) multiplexer_4 (.in0(multiplexer_1_out), .in1(adder_1_out), .out(NewPC), .sel(Relative));
  or or_1 (Flush, and_3_out, JR);

  // Other names for the same wires on the sheet: lane1_out[7:0] = fwd_lane1_out
endmodule

module Registrador_IF_ID (
  input  [31:0] ROM,
  input  [7:0] PC,
  input  Flush,
  input  Clock,
  input  rst,
  output [31:0] Decoder,
  output [7:0] PC1
);

  wire [39:0] multiplexer_1_out;

  Multiplexer #(.width(40)) multiplexer_1 (.in0({PC, ROM}), .in1(40'hffffffff), .out(multiplexer_1_out), .sel(Flush));
  Register #(.width(40)) register_1 (.D(multiplexer_1_out), .en(1'b1), .clk(Clock), .Q({PC1, Decoder}), .clr(rst));
endmodule

module Registrador_ID_EX (
  input  [7:0] L1_Ra,
  input  [7:0] L1_Rb,
  input  [7:0] L2_Ra,
  input  [7:0] L2_Rb,
  input  [7:0] L3_Ra,
  input  [7:0] L3_Rb,
  input  [7:0] L4_Ra,
  input  [7:0] L4_Rb,
  input  [7:0] PC1,
  input  [3:0] L2,
  input  [3:0] L1,
  input  [3:0] L4,
  input  [3:0] L3,
  input  [1:0] Rd_L4,
  input  [1:0] Rd_L3,
  input  [1:0] Rd_L1,
  input  Relative,
  input  JR,
  input  Branch,
  input  MUX_Imm,
  input  MUX_RegIn,
  input  L1RegWrite,
  input  MemWrite,
  input  MemRead,
  input  L4MUX_ULA_B,
  input  L4RegWrite,
  input  L3AluOp_0,
  input  L3AluOp_1,
  input  L3AluOp_2,
  input  L3MUX_ULA_B,
  input  L3RegWrite,
  input  L2Condition,
  input  Tipo_I_2,
  input  Tipo_I_L1,
  input  [1:0] Sel_Lane1,
  input  L4AluOp_0,
  input  L4AluOp_1,
  input  L4AluOp_2,
  input  CLK,
  input  Flush,
  input  rst,
  output [7:0] L1_RaS,
  output [7:0] L1_RbS,
  output [7:0] L2_RaS,
  output [7:0] L2_RbS,
  output [7:0] L3_RaS,
  output [7:0] L3_RbS,
  output [7:0] L4_RaS,
  output [7:0] L4_RbS,
  output [7:0] PC1S,
  output [3:0] L2S,
  output [3:0] L1S,
  output [3:0] L4S,
  output [3:0] L3S,
  output [1:0] Rd_L4S,
  output [1:0] Rd_L3S,
  output [1:0] Rd_L1S,
  output RelativeS,
  output JRS,
  output BranchS,
  output MUX_ImmS,
  output MUX_RegInS,
  output L1RegWriteS,
  output MemWriteS,
  output MemReadS,
  output L4MUX_ULA_BS,
  output L4Reg_WriteS,
  output L3ALUOp_0S,
  output L3ALUOp_1S,
  output L3ALUOp_2S,
  output L3MUX_ULA_BS,
  output L3RegWriteS,
  output L2ConditionS,
  output Tipo_I_L2S,
  output Tipo_I_L1S,
  output [1:0] Sel_lane1S,
  output L4ALUOp_0S,
  output L4ALUOp_1S,
  output L4ALUOp_2S
);

  wire [0:0] RegO_q;
  wire [1:0] RegL_q;
  wire [7:0] multiplexer_1_out, multiplexer_2_out, multiplexer_3_out, multiplexer_4_out, multiplexer_5_out,
       multiplexer_6_out, multiplexer_7_out, multiplexer_8_out, multiplexer_9_out, multiplexer_10_out,
       multiplexer_11_out, multiplexer_12_out, multiplexer_13_out, multiplexer_14_out, multiplexer_15_out;

  Multiplexer #(.width(8)) multiplexer_1 (.in0(L1_Ra), .in1({8{1'b0}}), .out(multiplexer_1_out), .sel(Flush));
  Multiplexer #(.width(8)) multiplexer_2 (.in0(L1_Rb), .in1({8{1'b0}}), .out(multiplexer_2_out), .sel(Flush));
  Register RegA (.D(multiplexer_1_out), .en(1'b1), .clk(CLK), .Q(L1_RaS), .clr(rst));
  Register RegB (.D(multiplexer_2_out), .en(1'b1), .clk(CLK), .Q(L1_RbS), .clr(rst));
  Register RegC (.D(multiplexer_3_out), .en(1'b1), .clk(CLK), .Q(L2_RaS), .clr(rst));
  Multiplexer #(.width(8)) multiplexer_3 (.in0(L2_Ra), .in1({8{1'b0}}), .out(multiplexer_3_out), .sel(Flush));
  Register RegD (.D(multiplexer_4_out), .en(1'b1), .clk(CLK), .Q(L2_RbS), .clr(rst));
  Multiplexer #(.width(8)) multiplexer_4 (.in0(L2_Rb), .in1({8{1'b0}}), .out(multiplexer_4_out), .sel(Flush));
  Register RegE (.D(multiplexer_5_out), .en(1'b1), .clk(CLK), .Q(L3_RaS), .clr(rst));
  Multiplexer #(.width(8)) multiplexer_5 (.in0(L3_Ra), .in1({8{1'b0}}), .out(multiplexer_5_out), .sel(Flush));
  Register RegF (.D(multiplexer_6_out), .en(1'b1), .clk(CLK), .Q(L3_RbS), .clr(rst));
  Multiplexer #(.width(8)) multiplexer_6 (.in0(L3_Rb), .in1({8{1'b0}}), .out(multiplexer_6_out), .sel(Flush));
  Register RegG (.D(multiplexer_7_out), .en(1'b1), .clk(CLK), .Q(L4_RaS), .clr(rst));
  Multiplexer #(.width(8)) multiplexer_7 (.in0(L4_Ra), .in1({8{1'b0}}), .out(multiplexer_7_out), .sel(Flush));
  Register RegH (.D(multiplexer_8_out), .en(1'b1), .clk(CLK), .Q(L4_RbS), .clr(rst));
  Multiplexer #(.width(8)) multiplexer_8 (.in0(L4_Rb), .in1({8{1'b0}}), .out(multiplexer_8_out), .sel(Flush));
  Register RegI (.D(multiplexer_9_out), .en(1'b1), .clk(CLK), .Q(PC1S), .clr(rst));
  Multiplexer #(.width(8)) multiplexer_9 (.in0(PC1), .in1({8{1'b0}}), .out(multiplexer_9_out), .sel(Flush));
  Register RegJ (.D(multiplexer_10_out), .en(1'b1), .clk(CLK), .Q({L1S, L2S}), .clr(rst));
  Multiplexer #(.width(8)) multiplexer_10 (.in0({L1, L2}), .in1({8{1'b0}}), .out(multiplexer_10_out), .sel(Flush));
  Register RegK (.D(multiplexer_11_out), .en(1'b1), .clk(CLK), .Q({L3S, L4S}), .clr(rst));
  Multiplexer #(.width(8)) multiplexer_11 (.in0({L3, L4}), .in1({8{1'b0}}), .out(multiplexer_11_out), .sel(Flush));
  Register RegL (.D(multiplexer_12_out), .en(1'b1), .clk(CLK), .Q({Rd_L1S, Rd_L3S, Rd_L4S, RegL_q}), .clr(rst));
  Multiplexer #(.width(8)) multiplexer_12 (
    .in0({Rd_L1, Rd_L3, Rd_L4, 2'b00}), .in1({8{1'b0}}), .out(multiplexer_12_out), .sel(Flush));
  Register RegM (
    .D(multiplexer_13_out), .en(1'b1), .clk(CLK),
    .Q({MemReadS, MemWriteS, L1RegWriteS, MUX_RegInS, MUX_ImmS, BranchS, JRS, RelativeS}), .clr(rst));
  Multiplexer #(.width(8)) multiplexer_13 (
    .in0({MemRead, MemWrite, L1RegWrite, MUX_RegIn, MUX_Imm, Branch, JR, Relative}), .in1({8{1'b0}}),
    .out(multiplexer_13_out), .sel(Flush));
  Register RegN (
    .D(multiplexer_14_out), .en(1'b1), .clk(CLK),
    .Q({L2ConditionS, L3RegWriteS, L3MUX_ULA_BS, L3ALUOp_2S, L3ALUOp_1S, L3ALUOp_0S, L4Reg_WriteS, L4MUX_ULA_BS}),
    .clr(rst));
  Multiplexer #(.width(8)) multiplexer_14 (
    .in0({L2Condition, L3RegWrite, L3MUX_ULA_B, L3AluOp_2, L3AluOp_1, L3AluOp_0, L4RegWrite, L4MUX_ULA_B}),
    .in1({8{1'b0}}), .out(multiplexer_14_out), .sel(Flush));
  Register RegO (
    .D(multiplexer_15_out), .en(1'b1), .clk(CLK),
    .Q({L4ALUOp_2S, L4ALUOp_1S, L4ALUOp_0S, Sel_lane1S, Tipo_I_L1S, Tipo_I_L2S, RegO_q[0]}), .clr(rst));
  Multiplexer #(.width(8)) multiplexer_15 (
    .in0({L4AluOp_2, L4AluOp_1, L4AluOp_0, Sel_Lane1, Tipo_I_L1, Tipo_I_2, 1'b0}), .in1({8{1'b0}}),
    .out(multiplexer_15_out), .sel(Flush));
endmodule

module Registrador_EX_WB (
  input  [7:0] lane1_out,
  input  [7:0] ULA_A,
  input  [7:0] ULA_B,
  input  L1_MUX_RegIn,
  input  L1_RegWrite,
  input  [1:0] Rd_L4,
  input  [1:0] Rd_L3,
  input  [1:0] Rd_L1,
  input  Tipo_I_L1,
  input  Tipo_I_L2,
  input  L4_RegWrite,
  input  L3_RegWrite,
  input  CLK,
  input  rst,
  output [7:0] lane1_outS,
  output [7:0] ULA_AS,
  output [7:0] ULA_BS,
  output L1_MUX_RegInS,
  output L1_RegWriteS,
  output [1:0] Rd_L4S,
  output [1:0] Rd_L3S,
  output [1:0] Rd_L1S,
  output Tipo_I_L1S,
  output Tipo_I_L2S,
  output L4_RegWriteS,
  output L3_RegWriteS
);

  wire [3:0] RegE_q;

  Register RegA (.D(lane1_out), .en(1'b1), .clk(CLK), .Q(lane1_outS), .clr(rst));
  Register RegB (.D(ULA_A), .en(1'b1), .clk(CLK), .Q(ULA_AS), .clr(rst));
  Register RegC (.D(ULA_B), .en(1'b1), .clk(CLK), .Q(ULA_BS), .clr(rst));
  Register RegD (
    .D({Rd_L1, Rd_L3, Rd_L4, L1_RegWrite, L1_MUX_RegIn}), .en(1'b1), .clk(CLK),
    .Q({Rd_L1S, Rd_L3S, Rd_L4S, L1_RegWriteS, L1_MUX_RegInS}), .clr(rst));
  Register RegE (
    .D({L3_RegWrite, L4_RegWrite, Tipo_I_L2, Tipo_I_L1, 4'b0000}), .en(1'b1), .clk(CLK),
    .Q({L3_RegWriteS, L4_RegWriteS, Tipo_I_L2S, Tipo_I_L1S, RegE_q}), .clr(rst));
endmodule

module Decodificador (
  input  [31:0] Instr_32b,
  output [1:0] RdAddr_L1_Ra,
  output [1:0] RdAddr_L2_Ra,
  output [1:0] RdAddr_L3_Ra,
  output [1:0] RdAddr_L4_Ra,
  output [1:0] RdAddr_L1_Rb,
  output [1:0] RdAddr_L2_Rb,
  output [1:0] RdAddr_L3_Rb,
  output [1:0] RdAddr_L4_Rb,
  output [1:0] Rd_L1,
  output [1:0] Rd_L3,
  output [1:0] Rd_L4,
  output [3:0] Imm_L1,
  output [3:0] Imm_L2,
  output [3:0] Imm_L3,
  output [3:0] Imm_L4,
  output [1:0] Sel_lane1,
  output MUX_Imm,
  output MemRead,
  output MemWrite,
  output l1RegWrite,
  output Mux_RegIn,
  output Condition,
  output Relative,
  output JR,
  output Branch,
  output MUX_ULA_BL3,
  output RegWriteL3,
  output [2:0] ALUOpL3,
  output MUX_ULA_BL4,
  output RegWriteL4,
  output [2:0] ALUOpL4,
  output Tipo_I_lane1,
  output Tipo_i_lane2
);

  ROM #(.addrWidth(4), .dataWidth(7)) rom_1 (
    .addr(Instr_32b[31:28]), .data({Mux_RegIn, l1RegWrite, MemWrite, MemRead, MUX_Imm, Sel_lane1}));
  ROM #(.addrWidth(4), .dataWidth(4)) rom_2 (.addr(Instr_32b[23:20]), .data({Branch, JR, Relative, Condition}));
  ROM #(.addrWidth(4), .dataWidth(5)) rom_3 (.addr(Instr_32b[15:12]), .data({ALUOpL3, RegWriteL3, MUX_ULA_BL3}));
  ROM #(.addrWidth(4), .dataWidth(5)) rom_4 (.addr(Instr_32b[7:4]), .data({ALUOpL4, RegWriteL4, MUX_ULA_BL4}));
  Detector_tipo_I detector_tipo_i_1 (.Opcode(Instr_32b[31:28]), .is_I(Tipo_I_lane1));
  Detector_tipo_I detector_tipo_i_2 (.Opcode(Instr_32b[23:20]), .is_I(Tipo_i_lane2));

  assign Imm_L1 = Instr_32b[27:24];
  assign Imm_L2 = Instr_32b[19:16];
  assign Imm_L3 = Instr_32b[11:8];
  assign Imm_L4 = Instr_32b[3:0];
  assign Rd_L1 = Instr_32b[27:26];
  assign Rd_L3 = Instr_32b[11:10];
  assign Rd_L4 = Instr_32b[3:2];
  assign RdAddr_L1_Ra = Instr_32b[27:26];
  assign RdAddr_L1_Rb = Instr_32b[25:24];
  assign RdAddr_L2_Ra = Instr_32b[19:18];
  assign RdAddr_L2_Rb = Instr_32b[17:16];
  assign RdAddr_L3_Ra = Instr_32b[11:10];
  assign RdAddr_L3_Rb = Instr_32b[9:8];
  assign RdAddr_L4_Ra = Instr_32b[3:2];
  assign RdAddr_L4_Rb = Instr_32b[1:0];

  // Other names for the same wires on the sheet: Lane4_ULAB[7:0] = Instr_32b[7:0]; Rb_Lane4[1:0] = Instr_32b[1:0];
  //   Ra_Lane4[1:0] = Instr_32b[3:2]; Opcode_Lane4[3:0] = Instr_32b[7:4]; Lane3_ULAA[7:0] = Instr_32b[15:8];
  //   Rb_Lane3[1:0] = Instr_32b[9:8]; Ra_Lane3[1:0] = Instr_32b[11:10]; Opcode_Lane3[3:0] = Instr_32b[15:12];
  //   Lane2_Desvios[7:0] = Instr_32b[23:16]; Rb_Lane2[1:0] = Instr_32b[17:16]; Ra_Lane2[1:0] = Instr_32b[19:18];
  //   Opcode_Lane2[3:0] = Instr_32b[23:20]; Lane1_Memoria[7:0] = Instr_32b[31:24]; Rb_Lane1[1:0] = Instr_32b[25:24];
  //   Ra_Lane1[1:0] = Instr_32b[27:26]; Opcode_Lane1[3:0] = Instr_32b[31:28]

  // Notes on the sheet:
  //   contents of rom_1 (hex, n*v repeats v):
  //   4*3 28 13 65 61 3 3 62 5*3
  //   contents of rom_2 (hex, n*v repeats v):
  //   8 b 4
  //   contents of rom_3 (hex, n*v repeats v):
  //   1c 1c 1c 3 4*1c 2 6 1c a e 12 16 1c
  //   contents of rom_4 (hex, n*v repeats v):
  //   1c 1c 1c 3 4*1c 2 6 1c a e 12 16 1c
endmodule

module InstMem (
  input  [7:0] Address,
  output [31:0] InstOut
);

  ROM #(.dataWidth(32)) rom_1 (.addr(Address), .data(InstOut));

  // Notes on the sheet:
  //   contents of rom_1 (hex, n*v repeats v):
  //   61ffffff 78ffffff a8ffffff 60ffffff 70ffffff a4ffffff 60ffffff 7cffffff acffffff ffffffff ffffffff
  //   56ff3fff ffff39ff 60ffffff 71ffffff ff0cffff 60ffffff 7bffffff ff20ffff 60ffffff 70ffffff a8ffffff
  //   a4ffffff 60ffffff 7cffffff acffffff ffffffff ffffffff 56ff3fff ffff3935 60ffffff 72ffffff ff0cffff
  //   60ffffff 7cffffff ff20ffff 60ffffff 7cffffff a8ffffff 61ffffff 74ffffff a4ffffff 60ffffff 7cffffff
  //   acffffff ffffffff ffffffff 56ff3fff ffff3935 60ffffff 75ffffff ff0cffff 60ffffff 7fffffff ff20ffff
  //   60ffffff 7cffffff a4ffffff 61ffffff 78ffffff a8ffffff 60ffffff 7cffffff acffffff ffffffff ffffffff
  //   60ffffff 7cffffff ffffffff ffffffff ffffffff ffff93ff ffffffff ffffffff ffffffff 40ffffff ffffffff
  //   ffffffff ffffffff 45ffffff ffffffff ffffffff ffffffff ffff81ff ffffffff ffffffff ffffffff 52ffffff
  //   ffff3539 ffff3fff 66ffffff 70ffffff ff0cffff 64ffffff 72ffffff ff20ffff ffffffff
endmodule

module Detector_tipo_I (
  input  [3:0] Opcode,
  output is_I
);

  wire comparator_1_eq, comparator_2_eq, comparator_3_eq;

  Comparator #(.width(4)) comparator_1 (.a(Opcode), .b(4'b0110), .eq(comparator_1_eq));  // open: gt, lt
  Comparator #(.width(4)) comparator_2 (.a(Opcode), .b(4'b0111), .eq(comparator_2_eq));  // open: gt, lt
  Comparator #(.width(4)) comparator_3 (.a(Opcode), .b(4'b0001), .eq(comparator_3_eq));  // open: gt, lt
  or or_1 (is_I, comparator_1_eq, comparator_2_eq, comparator_3_eq);
endmodule

module Extensao_reg_id_ex (
  input  [1:0] RdAddr_l2_ra,
  input  [1:0] RdAddr_l2_rb,
  input  [1:0] RdAddr_l1_rb,
  input  CLK,
  input  Flush,
  input  rst,
  output [1:0] ra_l2_addr,
  output [1:0] rb_l2_addr,
  output [1:0] rb_addr
);

  wire [1:0] RegO_q;
  wire [7:0] multiplexer_1_out;

  Register RegO (.D(multiplexer_1_out), .en(1'b1), .clk(CLK), .Q({rb_addr, rb_l2_addr, ra_l2_addr, RegO_q}), .clr(rst));
  Multiplexer #(.width(8)) multiplexer_1 (
    .in0({RdAddr_l1_rb, RdAddr_l2_rb, RdAddr_l2_ra, 2'b00}), .in1({8{1'b0}}), .out(multiplexer_1_out),
    .sel(Flush));
endmodule
